// Logisim project Main.circ as structural Verilog: 6 circuits, main circuit main
module main (
);

  wire button_1_out, button_2_out, button_3_out, stage1_1_clock_enabled, stage4_1_clock_enable;
  wire [3:0] stage4_1_min_t, stage4_1_min_u, stage4_1_sec_t, stage4_1_sec_u, stage5_1_st1_mt,
       stage5_1_st1_mu, stage5_1_st1_st, stage5_1_st1_su, stage5_1_st2_mt, stage5_1_st2_mu, stage5_1_st2_st,
       stage5_1_st2_su, stage5_1_st3_mt, stage5_1_st3_mu, stage5_1_st3_st, stage5_1_st3_su, stage5_1_st4_mt,
       stage5_1_st4_mu, stage5_1_st4_st, stage5_1_st4_su, stage5_1_st5_mt, stage5_1_st5_mu, stage5_1_st5_st,
       stage5_1_st5_su;

  Hex_Digit_Display hex_digit_display_1 (.value(stage4_1_min_t));  // open: dp
  Hex_Digit_Display hex_digit_display_2 (.value(stage4_1_min_u));  // open: dp
  Button button_1 (.out(button_1_out));
  Hex_Digit_Display hex_digit_display_3 (.value(stage4_1_sec_t));  // open: dp
  Hex_Digit_Display hex_digit_display_4 (.value(stage4_1_sec_u));  // open: dp
  Button button_2 (.out(button_2_out));
  Button button_3 (.out(button_3_out));
  Hex_Digit_Display hex_digit_display_5 (.value(stage5_1_st1_mt));  // open: dp
  Hex_Digit_Display hex_digit_display_6 (.value(stage5_1_st1_mu));  // open: dp
  LED led_1 (.in(stage4_1_clock_enable));
  Hex_Digit_Display hex_digit_display_7 (.value(stage5_1_st1_st));  // open: dp
  Hex_Digit_Display hex_digit_display_8 (.value(stage5_1_st1_su));  // open: dp
  Stage1 stage1_1 (.Start_Stop(button_1_out), .Reset(button_3_out), .Clock_Enabled(stage1_1_clock_enabled));
  Stage4 stage4_1 (
    .Start_Stop(stage1_1_clock_enabled), .Reset(button_3_out), .SEC_U(stage4_1_sec_u),
    .SEC_T(stage4_1_sec_t), .MIN_U(stage4_1_min_u), .Clock_Enable(stage4_1_clock_enable),
    .MIN_T(stage4_1_min_t));
  Stage5 stage5_1 (
    .Start_Stop(stage1_1_clock_enabled), .Split(button_2_out), .Reset(button_3_out),
    .ST1_sU(stage5_1_st1_su), .ST1_sT(stage5_1_st1_st), .ST2_sU(stage5_1_st2_su), .ST2_sT(stage5_1_st2_st),
    .ST2_mU(stage5_1_st2_mu), .ST2_mT(stage5_1_st2_mt), .ST3_sU(stage5_1_st3_su), .ST1_mU(stage5_1_st1_mu),
    .ST3_sT(stage5_1_st3_st), .ST3_mU(stage5_1_st3_mu), .ST3_mT(stage5_1_st3_mt), .ST4_sU(stage5_1_st4_su),
    .ST4_sT(stage5_1_st4_st), .ST4_mU(stage5_1_st4_mu), .ST4_mT(stage5_1_st4_mt), .ST1_mT(stage5_1_st1_mt),
    .ST5_sU(stage5_1_st5_su), .ST5_sT(stage5_1_st5_st), .ST5_mU(stage5_1_st5_mu), .ST5_mT(stage5_1_st5_mt));
  Hex_Digit_Display hex_digit_display_9 (.value(stage5_1_st2_mt));  // open: dp
  Hex_Digit_Display hex_digit_display_10 (.value(stage5_1_st2_mu));  // open: dp
  Hex_Digit_Display hex_digit_display_11 (.value(stage5_1_st3_mt));  // open: dp
  Hex_Digit_Display hex_digit_display_12 (.value(stage5_1_st3_mu));  // open: dp
  Hex_Digit_Display hex_digit_display_13 (.value(stage5_1_st4_mt));  // open: dp
  Hex_Digit_Display hex_digit_display_14 (.value(stage5_1_st4_mu));  // open: dp
  Hex_Digit_Display hex_digit_display_15 (.value(stage5_1_st5_mt));  // open: dp
  Hex_Digit_Display hex_digit_display_16 (.value(stage5_1_st5_mu));  // open: dp
  Hex_Digit_Display hex_digit_display_17 (.value(stage5_1_st2_st));  // open: dp
  Hex_Digit_Display hex_digit_display_18 (.value(stage5_1_st3_st));  // open: dp
  Hex_Digit_Display hex_digit_display_19 (.value(stage5_1_st4_st));  // open: dp
  Hex_Digit_Display hex_digit_display_20 (.value(stage5_1_st5_st));  // open: dp
  Hex_Digit_Display hex_digit_display_21 (.value(stage5_1_st2_su));  // open: dp
  Hex_Digit_Display hex_digit_display_22 (.value(stage5_1_st3_su));  // open: dp
  Hex_Digit_Display hex_digit_display_23 (.value(stage5_1_st4_su));  // open: dp
  Hex_Digit_Display hex_digit_display_24 (.value(stage5_1_st5_su));  // open: dp

  // Notes on the sheet:
  //   Elapsed Time
  //   Minutes
  //   :
  //   Start / Stop
  //   Seconds
  //   Stopwatch Interface
  //   Split
  //   Reset
  //   Minutes
  //   Clock Started
  //   Split Time 1
  //   :
  //   Seconds
  //   Split Time 2
  //   :
  //   Split Time 3
  //   :
  //   Split Time 4
  //   Split Time 5
endmodule

module Stage1 (
  input  Start_Stop,
  input  Reset,
  output Clock_Enabled
);

  T_Flip_Flop t_ff_1 (.T(1'b1), .clk(Start_Stop), .Q(Clock_Enabled), .reset(Reset));  // open: Qn, preset
  LED Clock_Started (.in(Clock_Enabled));
endmodule

module Stage2 (
  input  Reset,
  input  Start_Stop,
  output Clock_Enable,
  output [3:0] S_U,
  output Reset_OP
);

  wire clock_1_out, or_1_out;

  J_K_Flip_Flop #(.trigger("falling")) JK0 (
    .J(Start_Stop), .K(Start_Stop), .clk(clock_1_out), .Q(S_U[0]), .reset(or_1_out));  // open: Qn, preset
  Clock clock_1 (.out(clock_1_out));
  or or_1 (or_1_out, Reset, Reset_OP);
  J_K_Flip_Flop #(.trigger("falling")) JK1 (
    .J(Start_Stop), .K(Start_Stop), .clk(S_U[0]), .Q(S_U[1]), .reset(or_1_out));  // open: Qn, preset
  J_K_Flip_Flop #(.trigger("falling")) JK2 (
    .J(Start_Stop), .K(Start_Stop), .clk(S_U[1]), .Q(S_U[2]), .reset(or_1_out));  // open: Qn, preset
  and and_1 (Reset_OP, S_U[1], S_U[3]);
  J_K_Flip_Flop #(.trigger("falling")) JK3 (
    .J(Start_Stop), .K(Start_Stop), .clk(S_U[2]), .Q(S_U[3]), .reset(or_1_out));  // open: Qn, preset
  LED Clock_Started (.in(Start_Stop));
  Hex_Digit_Display hex_digit_display_1 (.value(S_U));  // open: dp

  assign Clock_Enable = Start_Stop;

  // Notes on the sheet:
  //   Signal send to Stage 3
  //   Count to 9, reset at 10. = JK1 AND JK3
endmodule

module Stage3 (
  input  Reset,
  input  Start_Stop,
  output [3:0] S_U,
  output Clock_Enable,
  output [3:0] S_T,
  output Reset_OP
);

  wire not_1_out, or_1_out, stage2_1_reset_op;

  J_K_Flip_Flop #(.trigger("falling")) JK0 (
    .J(Clock_Enable), .K(Clock_Enable), .clk(stage2_1_reset_op), .Q(S_T[0]), .reset(or_1_out));  // open: Qn, preset
  or or_1 (or_1_out, Reset, Reset_OP);
  not not_1 (not_1_out, S_T[0]);
  Stage2 stage2_1 (
    .Reset(Reset), .Start_Stop(Start_Stop), .Clock_Enable(Clock_Enable), .S_U(S_U),
    .Reset_OP(stage2_1_reset_op));
  J_K_Flip_Flop #(.trigger("falling")) JK1 (
    .J(Clock_Enable), .K(Clock_Enable), .clk(S_T[0]), .Q(S_T[1]), .reset(or_1_out));  // open: Qn, preset
  and and_1 (Reset_OP, not_1_out, S_T[1], S_T[2]);
  J_K_Flip_Flop #(.trigger("falling")) JK2 (
    .J(Clock_Enable), .K(Clock_Enable), .clk(S_T[1]), .Q(S_T[2]), .reset(or_1_out));  // open: Qn, preset
  LED Clock_Started (.in(Clock_Enable));
  Hex_Digit_Display hex_digit_display_1 (.value({1'b0, S_T[2:0]}));  // open: dp
  Hex_Digit_Display hex_digit_display_2 (.value(S_U));  // open: dp

  assign S_T[3] = 1'b0;

  // Notes on the sheet:
  //   Signal send to Stage 4
  //   Count to 5, reset at 6.
endmodule

module Stage4 (
  input  Start_Stop,
  input  Reset,
  output [3:0] SEC_U,
  output [3:0] SEC_T,
  output [3:0] MIN_U,
  output Clock_Enable,
  output [3:0] MIN_T
);

  wire and_1_out, and_2_out, d_ff_1_q, d_ff_2_q, d_ff_3_q, d_ff_4_q, or_1_out, or_2_out, stage3_1_reset_op;

  D_Flip_Flop d_ff_1 (.D(1'b0), .clk(Reset), .Q(d_ff_1_q));  // open: Qn, preset, reset
  D_Flip_Flop d_ff_2 (.D(1'b0), .clk(Reset), .Q(d_ff_2_q));  // open: Qn, preset, reset
  D_Flip_Flop d_ff_3 (.D(1'b0), .clk(Reset), .Q(d_ff_3_q));  // open: Qn, preset, reset
  D_Flip_Flop d_ff_4 (.D(1'b1), .clk(Reset), .Q(d_ff_4_q));  // open: Qn, preset, reset
  LED A_R0 (.in(d_ff_1_q));
  LED A_R1 (.in(d_ff_2_q));
  LED A_R2 (.in(d_ff_3_q));
  LED A_R3 (.in(d_ff_4_q));
  J_K_Flip_Flop #(.trigger("falling")) U_JK0 (
    .J(Clock_Enable), .K(Clock_Enable), .clk(stage3_1_reset_op), .Q(MIN_U[0]), .reset(or_1_out));  // open: Qn, preset
  J_K_Flip_Flop #(.trigger("falling")) T_JK0 (
    .J(Clock_Enable), .K(Clock_Enable), .clk(and_1_out), .Q(MIN_T[0]), .reset(or_2_out));  // open: Qn, preset
  or or_1 (or_1_out, Reset, and_1_out);
  or or_2 (or_2_out, Reset, and_2_out);
  J_K_Flip_Flop #(.trigger("falling")) U_JK1 (
    .J(Clock_Enable), .K(Clock_Enable), .clk(MIN_U[0]), .Q(MIN_U[1]), .reset(or_1_out));  // open: Qn, preset
  J_K_Flip_Flop #(.trigger("falling")) T_JK1 (
    .J(Clock_Enable), .K(Clock_Enable), .clk(MIN_T[0]), .Q(MIN_T[1]), .reset(or_2_out));  // open: Qn, preset
  Stage3 stage3_1 (
    .Reset(Reset), .Start_Stop(Start_Stop), .S_U(SEC_U), .Clock_Enable(Clock_Enable), .S_T(SEC_T),
    .Reset_OP(stage3_1_reset_op));
  J_K_Flip_Flop #(.trigger("falling")) U_JK2 (
    .J(Clock_Enable), .K(Clock_Enable), .clk(MIN_U[1]), .Q(MIN_U[2]), .reset(or_1_out));  // open: Qn, preset
  J_K_Flip_Flop #(.trigger("falling")) T_JK2 (
    .J(Clock_Enable), .K(Clock_Enable), .clk(MIN_T[1]), .Q(MIN_T[2]), .reset(or_2_out));  // open: Qn, preset
  J_K_Flip_Flop #(.trigger("falling")) U_JK3 (
    .J(Clock_Enable), .K(Clock_Enable), .clk(MIN_U[2]), .Q(MIN_U[3]), .preset(Reset), .reset(and_1_out));  // open: Qn
  J_K_Flip_Flop #(.trigger("falling")) T_JK3 (
    .J(Clock_Enable), .K(Clock_Enable), .clk(MIN_T[2]), .Q(MIN_T[3]), .reset(or_2_out));  // open: Qn, preset
  and and_1 (and_1_out, MIN_U[1], MIN_U[3]);
  and and_2 (and_2_out, MIN_T[1], MIN_T[3]);
  LED Clock_Started (.in(Clock_Enable));
  Hex_Digit_Display hex_digit_display_1 (.value(MIN_U));  // open: dp
  Hex_Digit_Display hex_digit_display_2 (.value(MIN_T));  // open: dp
  Hex_Digit_Display hex_digit_display_3 (.value(SEC_T));  // open: dp
  Hex_Digit_Display hex_digit_display_4 (.value(SEC_U));  // open: dp

  // Notes on the sheet:
  //   Adjust the require index to reset
  //   Count to 9, reset at 10.
  //   Count to 9, reset at 10.
  //   :
endmodule

module Stage5 (
  input  Start_Stop,
  input  Split,
  input  Reset,
  output [3:0] ST1_sU,
  output [3:0] ST1_sT,
  output [3:0] ST2_sU,
  output [3:0] ST2_sT,
  output [3:0] ST2_mU,
  output [3:0] ST2_mT,
  output [3:0] ST3_sU,
  output [3:0] ST1_mU,
  output [3:0] ST3_sT,
  output [3:0] ST3_mU,
  output [3:0] ST3_mT,
  output [3:0] ST4_sU,
  output [3:0] ST4_sT,
  output [3:0] ST4_mU,
  output [3:0] ST4_mT,
  output [3:0] ST1_mT,
  output [3:0] ST5_sU,
  output [3:0] ST5_sT,
  output [3:0] ST5_mU,
  output [3:0] ST5_mT
);

  wire and_1_out, nand_1_out, S0_qn, S1_qn, S2_qn, stage4_1_clock_enable;
  wire [2:0] S2_q;
  wire [3:0] stage4_1_min_t, stage4_1_min_u, stage4_1_sec_t, stage4_1_sec_u;

  Hex_Digit_Display hex_digit_display_1 (.value(stage4_1_min_t));  // open: dp
  Hex_Digit_Display hex_digit_display_2 (.value(stage4_1_min_u));  // open: dp
  Hex_Digit_Display hex_digit_display_3 (.value(stage4_1_sec_t));  // open: dp
  Hex_Digit_Display hex_digit_display_4 (.value(stage4_1_sec_u));  // open: dp
  Hex_Digit_Display hex_digit_display_5 (.value(ST1_mT));  // open: dp
  Hex_Digit_Display hex_digit_display_6 (.value(ST1_mU));  // open: dp
  LED Clock_Started (.in(stage4_1_clock_enable));
  Hex_Digit_Display hex_digit_display_7 (.value(ST1_sT));  // open: dp
  Hex_Digit_Display hex_digit_display_8 (.value(ST1_sU));  // open: dp
  D_Flip_Flop S_U3 (.D(stage4_1_sec_u[3]), .clk(and_1_out), .Q(ST1_sU[3]), .reset(Reset));  // open: Qn, preset
  D_Flip_Flop S_T3 (.D(stage4_1_sec_t[3]), .clk(and_1_out), .Q(ST1_sT[3]), .reset(Reset));  // open: Qn, preset
  D_Flip_Flop M_U3 (.D(stage4_1_min_u[3]), .clk(and_1_out), .Q(ST1_mU[3]), .reset(Reset));  // open: Qn, preset
  D_Flip_Flop M_T3 (.D(stage4_1_min_t[3]), .clk(and_1_out), .Q(ST1_mT[3]), .reset(Reset));  // open: Qn, preset
  D_Flip_Flop S_U2 (.D(stage4_1_sec_u[2]), .clk(and_1_out), .Q(ST1_sU[2]), .reset(Reset));  // open: Qn, preset
  D_Flip_Flop S_T2 (.D(stage4_1_sec_t[2]), .clk(and_1_out), .Q(ST1_sT[2]), .reset(Reset));  // open: Qn, preset
  D_Flip_Flop M_U2 (.D(stage4_1_min_u[2]), .clk(and_1_out), .Q(ST1_mU[2]), .reset(Reset));  // open: Qn, preset
  D_Flip_Flop M_T2 (.D(stage4_1_min_t[2]), .clk(and_1_out), .Q(ST1_mT[2]), .reset(Reset));  // open: Qn, preset
  D_Flip_Flop S_U1 (.D(stage4_1_sec_u[1]), .clk(and_1_out), .Q(ST1_sU[1]), .reset(Reset));  // open: Qn, preset
  D_Flip_Flop S_T1 (.D(stage4_1_sec_t[1]), .clk(and_1_out), .Q(ST1_sT[1]), .reset(Reset));  // open: Qn, preset
  D_Flip_Flop M_U1 (.D(stage4_1_min_u[1]), .clk(and_1_out), .Q(ST1_mU[1]), .reset(Reset));  // open: Qn, preset
  D_Flip_Flop M_T1 (.D(stage4_1_min_t[1]), .clk(and_1_out), .Q(ST1_mT[1]), .reset(Reset));  // open: Qn, preset
  D_Flip_Flop S_U0 (.D(stage4_1_sec_u[0]), .clk(and_1_out), .Q(ST1_sU[0]), .reset(Reset));  // open: Qn, preset
  D_Flip_Flop S_T0 (.D(stage4_1_sec_t[0]), .clk(and_1_out), .Q(ST1_sT[0]), .reset(Reset));  // open: Qn, preset
  D_Flip_Flop M_U0 (.D(stage4_1_min_u[0]), .clk(and_1_out), .Q(ST1_mU[0]), .reset(Reset));  // open: Qn, preset
  D_Flip_Flop M_T0 (.D(stage4_1_min_t[0]), .clk(and_1_out), .Q(ST1_mT[0]), .reset(Reset));  // open: Qn, preset
  Stage4 stage4_1 (
    .Start_Stop(Start_Stop), .Reset(Reset), .SEC_U(stage4_1_sec_u), .SEC_T(stage4_1_sec_t),
    .MIN_U(stage4_1_min_u), .Clock_Enable(stage4_1_clock_enable), .MIN_T(stage4_1_min_t));
  and and_1 (and_1_out, Split, nand_1_out);
  D_Flip_Flop S2 (.D(S2_qn), .clk(and_1_out), .Q(S2_q[0]), .Qn(S2_qn), .reset(Reset));  // open: preset
  Hex_Digit_Display hex_digit_display_9 (.value({1'b0, S2_q}));  // open: dp
  nand nand_1 (nand_1_out, S2_q[2], S2_q[0]);
  D_Flip_Flop S1 (.D(S1_qn), .clk(S2_qn), .Q(S2_q[1]), .Qn(S1_qn), .reset(Reset));  // open: preset
  D_Flip_Flop S0 (.D(S0_qn), .clk(S1_qn), .Q(S2_q[2]), .Qn(S0_qn), .reset(Reset));  // open: preset
  Register #(.width(4)) register_1 (.D(ST1_sU), .clk(and_1_out), .Q(ST2_sU), .clr(Reset));  // open: en
  Register #(.width(4)) register_2 (.D(ST1_sT), .clk(and_1_out), .Q(ST2_sT), .clr(Reset));  // open: en
  Register #(.width(4)) register_3 (.D(ST1_mU), .clk(and_1_out), .Q(ST2_mU), .clr(Reset));  // open: en
  Register #(.width(4)) register_4 (.D(ST1_mT), .clk(and_1_out), .Q(ST2_mT), .clr(Reset));  // open: en
  Hex_Digit_Display hex_digit_display_10 (.value(ST2_mT));  // open: dp
  Hex_Digit_Display hex_digit_display_11 (.value(ST2_mU));  // open: dp
  Hex_Digit_Display hex_digit_display_12 (.value(ST2_sT));  // open: dp
  Hex_Digit_Display hex_digit_display_13 (.value(ST2_sU));  // open: dp
  Register #(.width(4)) register_5 (.D(ST2_sU), .clk(and_1_out), .Q(ST3_sU), .clr(Reset));  // open: en
  Register #(.width(4)) register_6 (.D(ST2_sT), .clk(and_1_out), .Q(ST3_sT), .clr(Reset));  // open: en
  Register #(.width(4)) register_7 (.D(ST2_mU), .clk(and_1_out), .Q(ST3_mU), .clr(Reset));  // open: en
  Register #(.width(4)) register_8 (.D(ST2_mT), .clk(and_1_out), .Q(ST3_mT), .clr(Reset));  // open: en
  Hex_Digit_Display hex_digit_display_14 (.value(ST3_mT));  // open: dp
  Hex_Digit_Display hex_digit_display_15 (.value(ST3_mU));  // open: dp
  Hex_Digit_Display hex_digit_display_16 (.value(ST3_sT));  // open: dp
  Hex_Digit_Display hex_digit_display_17 (.value(ST3_sU));  // open: dp
  Register #(.width(4)) register_9 (.D(ST3_sU), .clk(and_1_out), .Q(ST4_sU), .clr(Reset));  // open: en
  Register #(.width(4)) register_10 (.D(ST3_sT), .clk(and_1_out), .Q(ST4_sT), .clr(Reset));  // open: en
  Register #(.width(4)) register_11 (.D(ST3_mU), .clk(and_1_out), .Q(ST4_mU), .clr(Reset));  // open: en
  Register #(.width(4)) register_12 (.D(ST3_mT), .clk(and_1_out), .Q(ST4_mT), .clr(Reset));  // open: en
  Hex_Digit_Display hex_digit_display_18 (.value(ST4_mT));  // open: dp
  Hex_Digit_Display hex_digit_display_19 (.value(ST4_mU));  // open: dp
  Hex_Digit_Display hex_digit_display_20 (.value(ST4_sT));  // open: dp
  Hex_Digit_Display hex_digit_display_21 (.value(ST4_sU));  // open: dp
  Register #(.width(4)) register_13 (.D(ST4_sU), .clk(and_1_out), .Q(ST5_sU), .clr(Reset));  // open: en
  Register #(.width(4)) register_14 (.D(ST4_sT), .clk(and_1_out), .Q(ST5_sT), .clr(Reset));  // open: en
  Register #(.width(4)) register_15 (.D(ST4_mU), .clk(and_1_out), .Q(ST5_mU), .clr(Reset));  // open: en
  Register #(.width(4)) register_16 (.D(ST4_mT), .clk(and_1_out), .Q(ST5_mT), .clr(Reset));  // open: en
  Hex_Digit_Display hex_digit_display_22 (.value(ST5_mT));  // open: dp
  Hex_Digit_Display hex_digit_display_23 (.value(ST5_mU));  // open: dp
  Hex_Digit_Display hex_digit_display_24 (.value(ST5_sT));  // open: dp
  Hex_Digit_Display hex_digit_display_25 (.value(ST5_sU));  // open: dp

  // Notes on the sheet:
  //   Elapsed Time
  //   Minutes
  //   :
  //   Seconds
  //   Minutes
  //   Split Time
  //   :
  //   Seconds
  //   Limit of 5 SPLIT clicks
  //   Minutes
  //   Split Time 2
  //   Seconds
  //   :
  //   Minutes
  //   Split Time 3
  //   Seconds
  //   :
  //   Minutes
  //   Split Time 4
  //   :
  //   Seconds
  //   Minutes
  //   Split Time 5
  //   :
  //   Seconds
endmodule
