// Logisim project Stage2.circ as structural Verilog: 3 circuits, main circuit main
module main (
);

  Hex_Digit_Display hex_digit_display_1 ();  // open: value, dp
  Hex_Digit_Display hex_digit_display_2 ();  // open: value, dp
  Button button_1 ();  // open: out
  Hex_Digit_Display hex_digit_display_3 ();  // open: value, dp
  Hex_Digit_Display hex_digit_display_4 ();  // open: value, dp
  Button button_2 ();  // open: out
  Button button_3 ();  // open: out
  Hex_Digit_Display hex_digit_display_5 ();  // open: value, dp
  Hex_Digit_Display hex_digit_display_6 ();  // open: value, dp
  LED led_1 ();  // open: in
  Hex_Digit_Display hex_digit_display_7 ();  // open: value, dp
  Hex_Digit_Display hex_digit_display_8 ();  // open: value, dp

  // Notes on the sheet:
  //   Elapsed Time
  //   Minutes
  //   :
  //   Start / Stop
  //   Seconds
  //   Stopwatch Interface
  //   Split
  //   Reset
  //   Minutes
  //   Clock Started
  //   Split Time
  //   :
  //   Seconds
endmodule

module Stage1 (
  input  Start_Stop,
  input  Reset,
  output Clock_Enabled
);

  T_Flip_Flop t_ff_1 (.T(1'b1), .clk(Start_Stop), .Q(Clock_Enabled), .reset(Reset));  // open: Qn, preset
  LED Clock_Started (.in(Clock_Enabled));
endmodule

module Stage2 (
  input  Reset,
  input  Start_Stop,
  output Clock_Enable,
  output [3:0] S_U,
  output Reset_OP
);

  wire clock_1_out, or_1_out;

  J_K_Flip_Flop #(.trigger("falling")) JK0 (
    .J(Start_Stop), .K(Start_Stop), .clk(clock_1_out), .Q(S_U[0]), .reset(or_1_out));  // open: Qn, preset
  Clock clock_1 (.out(clock_1_out));
  or or_1 (or_1_out, Reset, Reset_OP);
  J_K_Flip_Flop #(.trigger("falling")) JK1 (
    .J(Start_Stop), .K(Start_Stop), .clk(S_U[0]), .Q(S_U[1]), .reset(or_1_out));  // open: Qn, preset
  J_K_Flip_Flop #(.trigger("falling")) JK2 (
    .J(Start_Stop), .K(Start_Stop), .clk(S_U[1]), .Q(S_U[2]), .reset(or_1_out));  // open: Qn, preset
  and and_1 (Reset_OP, S_U[1], S_U[3]);
  J_K_Flip_Flop #(.trigger("falling")) JK3 (
    .J(Start_Stop), .K(Start_Stop), .clk(S_U[2]), .Q(S_U[3]), .reset(or_1_out));  // open: Qn, preset
  LED Clock_Started (.in(Start_Stop));
  Hex_Digit_Display hex_digit_display_1 (.value(S_U));  // open: dp

  assign Clock_Enable = Start_Stop;

  // Notes on the sheet:
  //   Signal send to Stage 3
  //   Count to 9, reset at 10. = JK1 AND JK3
endmodule
