// Logisim project Stage4.circ as structural Verilog: 5 circuits, main circuit main
module main (
);

  Hex_Digit_Display hex_digit_display_1 ();  // open: value, dp
  Hex_Digit_Display hex_digit_display_2 ();  // open: value, dp
  Button button_1 ();  // open: out
  Hex_Digit_Display hex_digit_display_3 ();  // open: value, dp
  Hex_Digit_Display hex_digit_display_4 ();  // open: value, dp
  Button button_2 ();  // open: out
  Button button_3 ();  // open: out
  Hex_Digit_Display hex_digit_display_5 ();  // open: value, dp
  Hex_Digit_Display hex_digit_display_6 ();  // open: value, dp
  LED led_1 ();  // open: in
  Hex_Digit_Display hex_digit_display_7 ();  // open: value, dp
  Hex_Digit_Display hex_digit_display_8 ();  // open: value, dp

  // Notes on the sheet:
  //   Elapsed Time
  //   Minutes
  //   :
  //   Start / Stop
  //   Seconds
  //   Stopwatch Interface
  //   Split
  //   Reset
  //   Minutes
  //   Clock Started
  //   Split Time
  //   :
  //   Seconds
endmodule

module Stage1 (
  input  Start_Stop,
  input  Reset,
  output Clock_Enabled
);

  T_Flip_Flop t_ff_1 (.T(1'b1), .clk(Start_Stop), .Q(Clock_Enabled), .reset(Reset));  // open: Qn, preset
  LED Clock_Started (.in(Clock_Enabled));
endmodule

module Stage2 (
  input  Reset,
  input  Start_Stop,
  output Clock_Enable,
  output [3:0] S_U,
  output Reset_OP
);

  wire clock_1_out, or_1_out;

  J_K_Flip_Flop #(.trigger("falling")) JK0 (
    .J(Start_Stop), .K(Start_Stop), .clk(clock_1_out), .Q(S_U[0]), .reset(or_1_out));  // open: Qn, preset
  Clock clock_1 (.out(clock_1_out));
  or or_1 (or_1_out, Reset, Reset_OP);
  J_K_Flip_Flop #(.trigger("falling")) JK1 (
    .J(Start_Stop), .K(Start_Stop), .clk(S_U[0]), .Q(S_U[1]), .reset(or_1_out));  // open: Qn, preset
  J_K_Flip_Flop #(.trigger("falling")) JK2 (
    .J(Start_Stop), .K(Start_Stop), .clk(S_U[1]), .Q(S_U[2]), .reset(or_1_out));  // open: Qn, preset
  and and_1 (Reset_OP, S_U[1], S_U[3]);
  J_K_Flip_Flop #(.trigger("falling")) JK3 (
    .J(Start_Stop), .K(Start_Stop), .clk(S_U[2]), .Q(S_U[3]), .reset(or_1_out));  // open: Qn, preset
  LED Clock_Started (.in(Start_Stop));
  Hex_Digit_Display hex_digit_display_1 (.value(S_U));  // open: dp

  assign Clock_Enable = Start_Stop;

  // Notes on the sheet:
  //   Signal send to Stage 3
  //   Count to 9, reset at 10. = JK1 AND JK3
endmodule

module Stage3 (
  input  Reset,
  input  Start_Stop,
  output [3:0] S_U,
  output Clock_Enable,
  output [3:0] S_T,
  output Reset_OP
);

  wire not_1_out, or_1_out, stage2_1_reset_op;

  J_K_Flip_Flop #(.trigger("falling")) JK0 (
    .J(Clock_Enable), .K(Clock_Enable), .clk(stage2_1_reset_op), .Q(S_T[0]), .reset(or_1_out));  // open: Qn, preset
  or or_1 (or_1_out, Reset, Reset_OP);
  not not_1 (not_1_out, S_T[0]);
  Stage2 stage2_1 (
    .Reset(Reset), .Start_Stop(Start_Stop), .Clock_Enable(Clock_Enable), .S_U(S_U),
    .Reset_OP(stage2_1_reset_op));
  J_K_Flip_Flop #(.trigger("falling")) JK1 (
    .J(Clock_Enable), .K(Clock_Enable), .clk(S_T[0]), .Q(S_T[1]), .reset(or_1_out));  // open: Qn, preset
  and and_1 (Reset_OP, not_1_out, S_T[1], S_T[2]);
  J_K_Flip_Flop #(.trigger("falling")) JK2 (
    .J(Clock_Enable), .K(Clock_Enable), .clk(S_T[1]), .Q(S_T[2]), .reset(or_1_out));  // open: Qn, preset
  LED Clock_Started (.in(Clock_Enable));
  Hex_Digit_Display hex_digit_display_1 (.value({1'b0, S_T[2:0]}));  // open: dp
  Hex_Digit_Display hex_digit_display_2 (.value(S_U));  // open: dp

  assign S_T[3] = 1'b0;

  // Notes on the sheet:
  //   Signal send to Stage 4
  //   Count to 5, reset at 6.
endmodule

module Stage4 (
  input  Start_Stop,
  input  Reset,
  output [3:0] SEC_U,
  output [3:0] SEC_T,
  output [3:0] MIN_U,
  output Clock_Enable,
  output [3:0] MIN_T
);

  wire and_1_out, and_2_out, d_ff_1_q, d_ff_2_q, d_ff_3_q, d_ff_4_q, or_1_out, or_2_out, stage3_1_reset_op;

  D_Flip_Flop d_ff_1 (.D(1'b0), .clk(Reset), .Q(d_ff_1_q));  // open: Qn, preset, reset
  D_Flip_Flop d_ff_2 (.D(1'b0), .clk(Reset), .Q(d_ff_2_q));  // open: Qn, preset, reset
  D_Flip_Flop d_ff_3 (.D(1'b0), .clk(Reset), .Q(d_ff_3_q));  // open: Qn, preset, reset
  D_Flip_Flop d_ff_4 (.D(1'b1), .clk(Reset), .Q(d_ff_4_q));  // open: Qn, preset, reset
  LED A_R0 (.in(d_ff_1_q));
  LED A_R1 (.in(d_ff_2_q));
  LED A_R2 (.in(d_ff_3_q));
  LED A_R3 (.in(d_ff_4_q));
  J_K_Flip_Flop #(.trigger("falling")) U_JK0 (
    .J(Clock_Enable), .K(Clock_Enable), .clk(stage3_1_reset_op), .Q(MIN_U[0]), .reset(or_1_out));  // open: Qn, preset
  J_K_Flip_Flop #(.trigger("falling")) T_JK0 (
    .J(Clock_Enable), .K(Clock_Enable), .clk(and_1_out), .Q(MIN_T[0]), .reset(or_2_out));  // open: Qn, preset
  or or_1 (or_1_out, Reset, and_1_out);
  or or_2 (or_2_out, Reset, and_2_out);
  J_K_Flip_Flop #(.trigger("falling")) U_JK1 (
    .J(Clock_Enable), .K(Clock_Enable), .clk(MIN_U[0]), .Q(MIN_U[1]), .reset(or_1_out));  // open: Qn, preset
  J_K_Flip_Flop #(.trigger("falling")) T_JK1 (
    .J(Clock_Enable), .K(Clock_Enable), .clk(MIN_T[0]), .Q(MIN_T[1]), .reset(or_2_out));  // open: Qn, preset
  Stage3 stage3_1 (
    .Reset(Reset), .Start_Stop(Start_Stop), .S_U(SEC_U), .Clock_Enable(Clock_Enable), .S_T(SEC_T),
    .Reset_OP(stage3_1_reset_op));
  J_K_Flip_Flop #(.trigger("falling")) U_JK2 (
    .J(Clock_Enable), .K(Clock_Enable), .clk(MIN_U[1]), .Q(MIN_U[2]), .reset(or_1_out));  // open: Qn, preset
  J_K_Flip_Flop #(.trigger("falling")) T_JK2 (
    .J(Clock_Enable), .K(Clock_Enable), .clk(MIN_T[1]), .Q(MIN_T[2]), .reset(or_2_out));  // open: Qn, preset
  J_K_Flip_Flop #(.trigger("falling")) U_JK3 (
    .J(Clock_Enable), .K(Clock_Enable), .clk(MIN_U[2]), .Q(MIN_U[3]), .preset(Reset), .reset(and_1_out));  // open: Qn
  J_K_Flip_Flop #(.trigger("falling")) T_JK3 (
    .J(Clock_Enable), .K(Clock_Enable), .clk(MIN_T[2]), .Q(MIN_T[3]), .reset(or_2_out));  // open: Qn, preset
  and and_1 (and_1_out, MIN_U[1], MIN_U[3]);
  and and_2 (and_2_out, MIN_T[1], MIN_T[3]);
  LED Clock_Started (.in(Clock_Enable));
  Hex_Digit_Display hex_digit_display_1 (.value(MIN_U));  // open: dp
  Hex_Digit_Display hex_digit_display_2 (.value(MIN_T));  // open: dp
  Hex_Digit_Display hex_digit_display_3 (.value(SEC_T));  // open: dp
  Hex_Digit_Display hex_digit_display_4 (.value(SEC_U));  // open: dp

  // Notes on the sheet:
  //   Adjust the require index to reset
  //   Count to 9, reset at 10.
  //   Count to 9, reset at 10.
  //   :
endmodule
