// Logisim project Stage3.circ as structural Verilog: 4 circuits, main circuit main
module main (
);

  Hex_Digit_Display hex_digit_display_1 ();  // open: value, dp
  Hex_Digit_Display hex_digit_display_2 ();  // open: value, dp
  Button button_1 ();  // open: out
  Hex_Digit_Display hex_digit_display_3 ();  // open: value, dp
  Hex_Digit_Display hex_digit_display_4 ();  // open: value, dp
  Button button_2 ();  // open: out
  Button button_3 ();  // open: out
  Hex_Digit_Display hex_digit_display_5 ();  // open: value, dp
  Hex_Digit_Display hex_digit_display_6 ();  // open: value, dp
  LED led_1 ();  // open: in
  Hex_Digit_Display hex_digit_display_7 ();  // open: value, dp
  Hex_Digit_Display hex_digit_display_8 ();  // open: value, dp

  // Notes on the sheet:
  //   Elapsed Time
  //   Minutes
  //   :
  //   Start / Stop
  //   Seconds
  //   Stopwatch Interface
  //   Split
  //   Reset
  //   Minutes
  //   Clock Started
  //   Split Time
  //   :
  //   Seconds
endmodule

module Stage1 (
  input  Start_Stop,
  input  Reset,
  output Clock_Enabled
);

  T_Flip_Flop t_ff_1 (.T(1'b1), .clk(Start_Stop), .Q(Clock_Enabled), .reset(Reset));  // open: Qn, preset
  LED Clock_Started (.in(Clock_Enabled));
endmodule

module Stage2 (
  input  Reset,
  input  Start_Stop,
  output Clock_Enable,
  output [3:0] S_U,
  output Reset_OP
);

  wire clock_1_out, or_1_out;

  J_K_Flip_Flop #(.trigger("falling")) JK0 (
    .J(Start_Stop), .K(Start_Stop), .clk(clock_1_out), .Q(S_U[0]), .reset(or_1_out));  // open: Qn, preset
  Clock clock_1 (.out(clock_1_out));
  or or_1 (or_1_out, Reset, Reset_OP);
  J_K_Flip_Flop #(.trigger("falling")) JK1 (
    .J(Start_Stop), .K(Start_Stop), .clk(S_U[0]), .Q(S_U[1]), .reset(or_1_out));  // open: Qn, preset
  J_K_Flip_Flop #(.trigger("falling")) JK2 (
    .J(Start_Stop), .K(Start_Stop), .clk(S_U[1]), .Q(S_U[2]), .reset(or_1_out));  // open: Qn, preset
  and and_1 (Reset_OP, S_U[1], S_U[3]);
  J_K_Flip_Flop #(.trigger("falling")) JK3 (
    .J(Start_Stop), .K(Start_Stop), .clk(S_U[2]), .Q(S_U[3]), .reset(or_1_out));  // open: Qn, preset
  LED Clock_Started (.in(Start_Stop));
  Hex_Digit_Display hex_digit_display_1 (.value(S_U));  // open: dp

  assign Clock_Enable = Start_Stop;

  // Notes on the sheet:
  //   Signal send to Stage 3
  //   Count to 9, reset at 10. = JK1 AND JK3
endmodule

module Stage3 (
  input  Reset,
  input  Start_Stop,
  output [3:0] S_U,
  output Clock_Enable,
  output [3:0] S_T,
  output Reset_OP
);

  wire not_1_out, or_1_out, stage2_1_reset_op;

  J_K_Flip_Flop #(.trigger("falling")) JK0 (
    .J(Clock_Enable), .K(Clock_Enable), .clk(stage2_1_reset_op), .Q(S_T[0]), .reset(or_1_out));  // open: Qn, preset
  or or_1 (or_1_out, Reset, Reset_OP);
  not not_1 (not_1_out, S_T[0]);
  Stage2 stage2_1 (
    .Reset(Reset), .Start_Stop(Start_Stop), .Clock_Enable(Clock_Enable), .S_U(S_U),
    .Reset_OP(stage2_1_reset_op));
  J_K_Flip_Flop #(.trigger("falling")) JK1 (
    .J(Clock_Enable), .K(Clock_Enable), .clk(S_T[0]), .Q(S_T[1]), .reset(or_1_out));  // open: Qn, preset
  and and_1 (Reset_OP, not_1_out, S_T[1], S_T[2]);
  J_K_Flip_Flop #(.trigger("falling")) JK2 (
    .J(Clock_Enable), .K(Clock_Enable), .clk(S_T[1]), .Q(S_T[2]), .reset(or_1_out));  // open: Qn, preset
  LED Clock_Started (.in(Clock_Enable));
  Hex_Digit_Display hex_digit_display_1 (.value({1'b0, S_T[2:0]}));  // open: dp
  Hex_Digit_Display hex_digit_display_2 (.value(S_U));  // open: dp

  assign S_T[3] = 1'b0;

  // Notes on the sheet:
  //   Signal send to Stage 4
  //   Count to 5, reset at 6.
endmodule
